// Logisim project practica3.circ as structural Verilog
module main (
  input  A,
  input  B,
  input  A_2,
  input  B_2,
  output salida,
  output salida_2
);

  wire transistor_1_out;

  Transistor #(.\type ("n")) transistor_1 (.in(1'b1), .out(transistor_1_out), .gate(A));
  Transistor #(.\type ("n")) transistor_2 (.in(transistor_1_out), .out(salida), .gate(B));
  Transistor transistor_3 (.in(1'b0), .out(salida), .gate(B));
  Transistor #(.\type ("n")) transistor_4 (.in(1'b1), .out(salida_2), .gate(A_2));
  Transistor #(.\type ("n")) transistor_5 (.in(1'b1), .out(salida_2), .gate(B_2));
  Transistor transistor_6 (.in(1'b0), .out(salida), .gate(A));
  Pull_Resistor pull_resistor_1 (.node(salida_2));

  // Notes on the sheet:
  //   Compuerta lógica AND con transitores 
  //   Compuerta lógica OR con transitores 
  //   Q1
  //   Q2
  //   Q3
  //   Q4
  //   Q1
  //   Q2
endmodule

module SI_y_solo_SI (
  input  A,
  input  B,
  output salida
);

  wire and_1_out, and_2_out, not_1_out, not_2_out;

  not not_1 (not_1_out, A);
  not not_2 (not_2_out, B);
  and and_1 (and_1_out, not_1_out, not_2_out);
  and and_2 (and_2_out, A, B);
  or or_1 (salida, and_1_out, and_2_out);

  // Notes on the sheet:
  //   SI y solo SI con compuertas lógicas 
endmodule

module Comparador_electronico (
  input  X,
  input  Y,
  output X___Y,
  output X___Y_2,
  output X___Y_3
);

  wire not_1_out, not_2_out, or_1_out;

  not not_1 (not_1_out, X);
  not not_2 (not_2_out, Y);
  and and_1 (X___Y, not_1_out, Y);
  and and_2 (X___Y_3, X, not_2_out);
  or or_1 (or_1_out, X___Y, X___Y_3);
  not not_3 (X___Y_2, or_1_out);

  // Notes on the sheet:
  //   Comparador electronico de 2 bits  
endmodule

module Mapas_de_Karnaugh (
  input  A,
  input  B,
  input  C,
  input  D,
  output X____Y
);

  wire and_1_out, and_2_out, and_3_out, and_4_out, and_5_out, not_1_out, not_2_out;

  not not_1 (not_1_out, C);
  not not_2 (not_2_out, D);
  and and_1 (and_1_out, A, not_2_out);
  and and_2 (and_2_out, A, B);
  and and_3 (and_3_out, A, not_1_out);
  and and_4 (and_4_out, B, not_1_out);
  and and_5 (and_5_out, not_1_out, not_2_out);
  or or_1 (X____Y, and_1_out, and_2_out, and_3_out, and_4_out, and_5_out);

  // Notes on the sheet:
  //   Mapa de Karnaugh
endmodule
