// Logisim project practica4.circ as structural Verilog
module Sumador_de_1_bit (
  input  C_in,
  input  A,
  input  B,
  output Suma,
  output Carry_Out
);

  wire and_1_out, and_2_out, xor_1_out;

  xor xor_1 (xor_1_out, A, B);
  and and_1 (and_1_out, B, A);
  xor xor_2 (Suma, C_in, xor_1_out);
  and and_2 (and_2_out, C_in, xor_1_out);
  or or_1 (Carry_Out, and_2_out, and_1_out);
  circuit part_1 ();

  // Notes on the sheet:
  //   FULL ADDER
endmodule

module Sumador_8_bits (
  input  C_in,
  input  [7:0] A,
  input  [7:0] B,
  output [7:0] out_4
);

  wire sumador_de_1_bit_1_carry_out, sumador_de_1_bit_2_carry_out, sumador_de_1_bit_3_carry_out,
       sumador_de_1_bit_4_carry_out, sumador_de_1_bit_5_carry_out, sumador_de_1_bit_6_carry_out,
       sumador_de_1_bit_7_carry_out;

  Sumador_de_1_bit sumador_de_1_bit_1 (
    .C_in(C_in), .A(A[0]), .B(B[0]), .Suma(out_4[0]), .Carry_Out(sumador_de_1_bit_1_carry_out));
  Sumador_de_1_bit sumador_de_1_bit_2 (
    .C_in(sumador_de_1_bit_1_carry_out), .A(A[1]), .B(B[1]), .Suma(out_4[1]),
    .Carry_Out(sumador_de_1_bit_2_carry_out));
  Sumador_de_1_bit sumador_de_1_bit_3 (
    .C_in(sumador_de_1_bit_2_carry_out), .A(A[2]), .B(B[2]), .Suma(out_4[2]),
    .Carry_Out(sumador_de_1_bit_3_carry_out));
  Sumador_de_1_bit sumador_de_1_bit_4 (
    .C_in(sumador_de_1_bit_3_carry_out), .A(A[3]), .B(B[3]), .Suma(out_4[3]),
    .Carry_Out(sumador_de_1_bit_4_carry_out));
  Sumador_de_1_bit sumador_de_1_bit_5 (
    .C_in(sumador_de_1_bit_4_carry_out), .A(A[4]), .B(B[4]), .Suma(out_4[4]),
    .Carry_Out(sumador_de_1_bit_5_carry_out));
  Sumador_de_1_bit sumador_de_1_bit_6 (
    .C_in(sumador_de_1_bit_5_carry_out), .A(A[5]), .B(B[5]), .Suma(out_4[5]),
    .Carry_Out(sumador_de_1_bit_6_carry_out));
  Sumador_de_1_bit sumador_de_1_bit_7 (
    .C_in(sumador_de_1_bit_6_carry_out), .A(A[6]), .B(B[6]), .Suma(out_4[6]),
    .Carry_Out(sumador_de_1_bit_7_carry_out));
  Sumador_de_1_bit sumador_de_1_bit_8 (
    .C_in(sumador_de_1_bit_7_carry_out), .A(A[7]), .B(B[7]), .Suma(out_4[7]));  // open: Carry_Out

  // Notes on the sheet:
  //   SUMADOR DE 8 BITS
  //   Suma
endmodule

module Restador_de_1_bit (
  input  C_in,
  input  A,
  input  B,
  output Resta,
  output Carry_Out
);

  wire and_1_out, and_2_out, not_1_out, not_2_out, xor_1_out;

  xor xor_1 (xor_1_out, A, B);
  not not_1 (not_1_out, A);
  not not_2 (not_2_out, xor_1_out);
  and and_1 (and_1_out, B, not_1_out);
  xor xor_2 (Resta, C_in, xor_1_out);
  and and_2 (and_2_out, C_in, not_2_out);
  or or_1 (Carry_Out, and_2_out, and_1_out);

  // Notes on the sheet:
  //   FULL SUBSTRACTOR
endmodule

module Restador_8_bits (
  input  C_in,
  input  [7:0] A,
  input  [7:0] B,
  output [7:0] out_4
);

  wire restador_de_1_bit_1_carry_out, restador_de_1_bit_2_carry_out, restador_de_1_bit_3_carry_out,
       restador_de_1_bit_4_carry_out, restador_de_1_bit_5_carry_out, restador_de_1_bit_6_carry_out,
       restador_de_1_bit_7_carry_out;

  Restador_de_1_bit restador_de_1_bit_1 (
    .C_in(C_in), .A(A[0]), .B(B[0]), .Resta(out_4[0]), .Carry_Out(restador_de_1_bit_1_carry_out));
  Restador_de_1_bit restador_de_1_bit_2 (
    .C_in(restador_de_1_bit_1_carry_out), .A(A[1]), .B(B[1]), .Resta(out_4[1]),
    .Carry_Out(restador_de_1_bit_2_carry_out));
  Restador_de_1_bit restador_de_1_bit_3 (
    .C_in(restador_de_1_bit_2_carry_out), .A(A[2]), .B(B[2]), .Resta(out_4[2]),
    .Carry_Out(restador_de_1_bit_3_carry_out));
  Restador_de_1_bit restador_de_1_bit_4 (
    .C_in(restador_de_1_bit_3_carry_out), .A(A[3]), .B(B[3]), .Resta(out_4[3]),
    .Carry_Out(restador_de_1_bit_4_carry_out));
  Restador_de_1_bit restador_de_1_bit_5 (
    .C_in(restador_de_1_bit_4_carry_out), .A(A[4]), .B(B[4]), .Resta(out_4[4]),
    .Carry_Out(restador_de_1_bit_5_carry_out));
  Restador_de_1_bit restador_de_1_bit_6 (
    .C_in(restador_de_1_bit_5_carry_out), .A(A[5]), .B(B[5]), .Resta(out_4[5]),
    .Carry_Out(restador_de_1_bit_6_carry_out));
  Restador_de_1_bit restador_de_1_bit_7 (
    .C_in(restador_de_1_bit_6_carry_out), .A(A[6]), .B(B[6]), .Resta(out_4[6]),
    .Carry_Out(restador_de_1_bit_7_carry_out));
  Restador_de_1_bit restador_de_1_bit_8 (
    .C_in(restador_de_1_bit_7_carry_out), .A(A[7]), .B(B[7]), .Resta(out_4[7]));  // open: Carry_Out

  // Notes on the sheet:
  //   RESTA DE 8 BITS
  //   Resta
endmodule

module Sumador_y_restador (
  input  in_1,
  input  [7:0] A,
  input  [7:0] in_3,
  input  in_4,
  output [7:0] out_5
);

  wire [7:0] restador_8_bits_1_out_4, sumador_8_bits_1_out_4;

  Sumador_8_bits sumador_8_bits_1 (.C_in(in_1), .A(A), .B(in_3), .out_4(sumador_8_bits_1_out_4));
  Restador_8_bits restador_8_bits_1 (.C_in(in_1), .A(A), .B(in_3), .out_4(restador_8_bits_1_out_4));
  Multiplexer #(.width(8)) multiplexer_1 (
    .in0(sumador_8_bits_1_out_4), .in1(restador_8_bits_1_out_4), .out(out_5), .sel(in_4));  // open: en

  // Notes on the sheet:
  //   ALU
  //   A
  //   Código de Operación
endmodule

module ALU_de_4_bits (
  input  C_i,
  input  [3:0] A,
  input  [3:0] B,
  input  [2:0] Suma_000,
  output [3:0] salida
);

  wire [3:0] AND_out, Compardor_salida, Equivalencia_salida, \Implicación_out_3 , OR_out, Restador_out_4,
       Sumador_out_4, XOR_out_3;

  sumador_4_bits Sumador (.C_in(C_i), .A(A), .B(B), .out_4(Sumador_out_4));
  XOR_de_4_bits XOR (.A(A), .B(B), .out_3(XOR_out_3));
  Comparador_4_bits Compardor (.E(C_i), .A(A), .B(B), .salida(Compardor_salida));
  \Implicación_4_bits  \Implicación  (.A(A), .B(B), .out_3(\Implicación_out_3 ));
  Equivalencia_4_bits Equivalencia (.A(A), .B(B), .salida(Equivalencia_salida));  // open: in_3
  R Restador (.C_in(C_i), .A(A), .B(B), .out_4(Restador_out_4));
  assign AND_out = A & B;  // AND_Gate AND, 4 bits wide
  assign OR_out = A | B;  // OR_Gate OR, 4 bits wide
  Multiplexer #(.select(3), .width(4)) multiplexer_1 (
    .in0(Sumador_out_4), .in1(Restador_out_4), .in2(AND_out), .in3(OR_out), .in4(XOR_out_3),
    .in5(Compardor_salida), .in6(\Implicación_out_3 ), .in7(Equivalencia_salida), .out(salida), .sel(Suma_000));  // open: en

  // Notes on the sheet:
  //   ALU
  //   Resta 001
  //   AND 010
  //   OR 011
  //   XOR 100
  //   Implicación 110
  //   Comparador 101
  //   Equivalencia 111
  //   Comparador
  //   A > B 0001
  //   A < B 0010
  //   A = B 0100
  //   Nota: Para el comparador es necesario que C_i sea igual a 1
  //   Equivalencia
  //   Si son iaguales 1
  //   Si son diferntes 0
endmodule

module sumador_4_bits (
  input  C_in,
  input  [3:0] A,
  input  [3:0] B,
  output [3:0] out_4
);

  wire sumador_de_1_bit_1_carry_out, sumador_de_1_bit_2_carry_out, sumador_de_1_bit_3_carry_out;

  Sumador_de_1_bit sumador_de_1_bit_1 (
    .C_in(C_in), .A(A[0]), .B(B[0]), .Suma(out_4[0]), .Carry_Out(sumador_de_1_bit_1_carry_out));
  Sumador_de_1_bit sumador_de_1_bit_2 (
    .C_in(sumador_de_1_bit_1_carry_out), .A(A[1]), .B(B[1]), .Suma(out_4[1]),
    .Carry_Out(sumador_de_1_bit_2_carry_out));
  Sumador_de_1_bit sumador_de_1_bit_3 (
    .C_in(sumador_de_1_bit_2_carry_out), .A(A[2]), .B(B[2]), .Suma(out_4[2]),
    .Carry_Out(sumador_de_1_bit_3_carry_out));
  Sumador_de_1_bit sumador_de_1_bit_4 (
    .C_in(sumador_de_1_bit_3_carry_out), .A(A[3]), .B(B[3]), .Suma(out_4[3]));  // open: Carry_Out

  // Notes on the sheet:
  //   sumador 4 bits
endmodule

module XOR (
  input  A,
  input  B,
  output salida
);

  xor xor_1 (salida, A, B);

  // Notes on the sheet:
  //   XOR
endmodule

module Comparador (
  input  A,
  input  B,
  input  E,
  output menor_A___B,
  output igual_A___B,
  output mayor_A___B
);

  wire and_1_out, and_2_out, not_1_out, not_2_out, not_3_out, xor_1_out;

  not not_1 (not_1_out, A);
  not not_2 (not_2_out, B);
  and and_1 (and_1_out, B, not_1_out);
  xor xor_1 (xor_1_out, A, B);
  and and_2 (and_2_out, A, not_2_out);
  not not_3 (not_3_out, xor_1_out);
  and and_3 (menor_A___B, and_1_out, E);
  and and_4 (igual_A___B, not_3_out, E);
  and and_5 (mayor_A___B, E, and_2_out);

  // Notes on the sheet:
  //   Comparador de 1 bit
endmodule

module XOR_de_4_bits (
  input  [3:0] A,
  input  [3:0] B,
  output [3:0] out_3
);

  XOR xor_1 (.A(A[0]), .B(B[0]), .salida(out_3[0]));
  XOR xor_2 (.A(A[1]), .B(B[1]), .salida(out_3[1]));
  XOR xor_3 (.A(A[2]), .B(B[2]), .salida(out_3[2]));
  XOR xor_4 (.A(A[3]), .B(B[3]), .salida(out_3[3]));

  // Notes on the sheet:
  //   XOR de 4 bits
endmodule

module Comparador_4_bits (
  input  E,
  input  [3:0] A,
  input  [3:0] B,
  output [3:0] salida
);

  wire and_1_out, and_2_out, and_3_out, and_4_out, and_5_out, and_6_out, comparador_1_igual_a___b,
       comparador_1_mayor_a___b, comparador_1_menor_a___b, comparador_2_igual_a___b,
       comparador_2_mayor_a___b, comparador_2_menor_a___b, comparador_3_igual_a___b,
       comparador_3_mayor_a___b, comparador_3_menor_a___b, comparador_4_igual_a___b,
       comparador_4_mayor_a___b, comparador_4_menor_a___b;

  Comparador comparador_1 (
    .A(A[3]), .B(B[3]), .E(E), .menor_A___B(comparador_1_menor_a___b),
    .igual_A___B(comparador_1_igual_a___b), .mayor_A___B(comparador_1_mayor_a___b));
  Comparador comparador_2 (
    .A(A[2]), .B(B[2]), .E(comparador_1_igual_a___b), .menor_A___B(comparador_2_menor_a___b),
    .igual_A___B(comparador_2_igual_a___b), .mayor_A___B(comparador_2_mayor_a___b));
  Comparador comparador_3 (
    .A(A[1]), .B(B[1]), .E(comparador_2_igual_a___b), .menor_A___B(comparador_3_menor_a___b),
    .igual_A___B(comparador_3_igual_a___b), .mayor_A___B(comparador_3_mayor_a___b));
  Comparador comparador_4 (
    .A(A[0]), .B(B[0]), .E(comparador_3_igual_a___b), .menor_A___B(comparador_4_menor_a___b),
    .igual_A___B(comparador_4_igual_a___b), .mayor_A___B(comparador_4_mayor_a___b));
  and and_1 (and_1_out, comparador_1_igual_a___b, comparador_2_mayor_a___b);
  and and_2 (and_2_out, comparador_1_igual_a___b, comparador_2_igual_a___b, comparador_3_mayor_a___b);
  and and_3 (and_3_out, comparador_1_igual_a___b, comparador_2_igual_a___b, comparador_3_igual_a___b, comparador_4_mayor_a___b);
  and and_4 (and_4_out, comparador_1_igual_a___b, comparador_2_menor_a___b);
  and and_5 (and_5_out, comparador_1_igual_a___b, comparador_2_igual_a___b, comparador_3_menor_a___b);
  and and_6 (and_6_out, comparador_1_igual_a___b, comparador_2_igual_a___b, comparador_3_igual_a___b, comparador_4_menor_a___b);
  or or_1 (salida[0], comparador_1_mayor_a___b, and_1_out, and_2_out, and_3_out);
  or or_2 (salida[1], comparador_1_menor_a___b, and_4_out, and_5_out, and_6_out);
  and and_7 (salida[2], comparador_1_igual_a___b, comparador_2_igual_a___b, comparador_3_igual_a___b, comparador_4_igual_a___b);

  // Notes on the sheet:
  //   Comparador 4 bits
  //   E debe estar prendido
  //   A > B mayor 
  //   A < B menor 
  //   A = B igual
  //   A>B es 0001
  //   A<B es 0010
  //   A=B es 0100
endmodule

module \Implicación_4_bits  (
  input  [3:0] A,
  input  [3:0] B,
  output [3:0] out_3
);

  wire [3:0] not_1_out;

  assign not_1_out = ~A;  // NOT_Gate not_1, 4 bits wide
  or or_1 (out_3[0], not_1_out[0], B[0]);
  or or_2 (out_3[1], not_1_out[1], B[1]);
  or or_3 (out_3[2], not_1_out[2], B[2]);
  or or_4 (out_3[3], not_1_out[3], B[3]);

  // Notes on the sheet:
  //   Implicación
endmodule

module Equivalencia_1_bit (
  input  A,
  input  B,
  output salida
);

  wire xor_1_out;

  xor xor_1 (xor_1_out, A, B);
  not not_1 (salida, xor_1_out);

  // Notes on the sheet:
  //   Equivalencia 1 bit
endmodule

module Equivalencia_4_bits (
  input  [3:0] A,
  input  [3:0] B,
  input  in_3,
  output [3:0] salida
);

  wire equivalencia_1_bit_1_salida, equivalencia_1_bit_2_salida, equivalencia_1_bit_3_salida,
       equivalencia_1_bit_4_salida;

  Equivalencia_1_bit equivalencia_1_bit_1 (.A(A[0]), .B(B[0]), .salida(equivalencia_1_bit_1_salida));
  Equivalencia_1_bit equivalencia_1_bit_2 (.A(A[1]), .B(B[1]), .salida(equivalencia_1_bit_2_salida));
  Equivalencia_1_bit equivalencia_1_bit_3 (.A(A[2]), .B(B[2]), .salida(equivalencia_1_bit_3_salida));
  Equivalencia_1_bit equivalencia_1_bit_4 (.A(A[3]), .B(B[3]), .salida(equivalencia_1_bit_4_salida));
  and and_1 (salida[0], equivalencia_1_bit_1_salida, equivalencia_1_bit_2_salida, equivalencia_1_bit_3_salida, equivalencia_1_bit_4_salida);

  assign salida[3:1] = {3{in_3}};

  // Notes on the sheet:
  //   Equivalencia 4 bits
  //   A igual B
  //   A diferenteB
endmodule

module R (
  input  C_in,
  input  [3:0] A,
  input  [3:0] B,
  output [3:0] out_4
);

  wire restador_de_1_bit_1_carry_out, restador_de_1_bit_2_carry_out, restador_de_1_bit_3_carry_out;

  Restador_de_1_bit restador_de_1_bit_1 (
    .C_in(C_in), .A(A[0]), .B(B[0]), .Resta(out_4[0]), .Carry_Out(restador_de_1_bit_1_carry_out));
  Restador_de_1_bit restador_de_1_bit_2 (
    .C_in(restador_de_1_bit_1_carry_out), .A(A[1]), .B(B[1]), .Resta(out_4[1]),
    .Carry_Out(restador_de_1_bit_2_carry_out));
  Restador_de_1_bit restador_de_1_bit_3 (
    .C_in(restador_de_1_bit_2_carry_out), .A(A[2]), .B(B[2]), .Resta(out_4[2]),
    .Carry_Out(restador_de_1_bit_3_carry_out));
  Restador_de_1_bit restador_de_1_bit_4 (
    .C_in(restador_de_1_bit_3_carry_out), .A(A[3]), .B(B[3]), .Resta(out_4[3]));  // open: Carry_Out

  // Notes on the sheet:
  //   Restador
endmodule
