// Logisim project practica5.circ as structural Verilog: 5 circuits, main circuit Ejercicio1
module Ejercicio1 (
  input  IN
);

  wire and_1_out, and_2_out, and_3_out, not_1_out, Reloj_out, S_0_qn, S_L_qn;
  wire [1:0] S_L_q;

  Clock Reloj (.out(Reloj_out));
  not not_1 (not_1_out, IN);
  S_R_Flip_Flop S_0 (
    .S(and_1_out), .clk(Reloj_out), .R(and_2_out), .Q(S_L_q[1]), .Qn(S_0_qn));  // open: preset, reset, en
  S_R_Flip_Flop S_L (
    .S(and_3_out), .clk(Reloj_out), .R(S_L_q[0]), .Q(S_L_q[0]), .Qn(S_L_qn));  // open: preset, reset, en
  and and_1 (and_1_out, not_1_out, S_0_qn, S_L_q[0]);
  and and_2 (and_2_out, not_1_out, S_L_q[1], S_L_q[0]);
  and and_3 (and_3_out, not_1_out, S_L_qn);
  Hex_Digit_Display hex_digit_display_1 (.value({2'b00, S_L_q}));  // open: dp

  // Notes on the sheet:
  //   Automata Simulator
endmodule

module Ejercicio2 (
  input  Reloj,
  input  [7:0] Register_in,
  input  Control_de_escritura,
  output [7:0] Resultado
);

  wire and_1_out, and_2_out, and_3_out, and_4_out, and_5_out, and_6_out, and_7_out, and_8_out;

  and and_1 (and_1_out, Register_in[0], Control_de_escritura);
  and and_2 (and_2_out, Register_in[1], Control_de_escritura);
  and and_3 (and_3_out, Register_in[2], Control_de_escritura);
  and and_4 (and_4_out, Register_in[3], Control_de_escritura);
  and and_5 (and_5_out, Register_in[4], Control_de_escritura);
  and and_6 (and_6_out, Register_in[5], Control_de_escritura);
  and and_7 (and_7_out, Register_in[6], Control_de_escritura);
  and and_8 (and_8_out, Register_in[7], Control_de_escritura);
  D_Flip_Flop d_ff_1 (.clk(Reloj), .D(and_1_out), .Q(Resultado[0]));  // open: Qn, preset, en, reset
  D_Flip_Flop d_ff_2 (.clk(Reloj), .D(and_2_out), .Q(Resultado[1]));  // open: Qn, preset, en, reset
  D_Flip_Flop d_ff_3 (.clk(Reloj), .D(and_3_out), .Q(Resultado[2]));  // open: Qn, preset, en, reset
  D_Flip_Flop d_ff_4 (.clk(Reloj), .D(and_4_out), .Q(Resultado[3]));  // open: Qn, preset, en, reset
  D_Flip_Flop d_ff_5 (.clk(Reloj), .D(and_5_out), .Q(Resultado[4]));  // open: Qn, preset, en, reset
  D_Flip_Flop d_ff_6 (.clk(Reloj), .D(and_6_out), .Q(Resultado[5]));  // open: Qn, preset, en, reset
  D_Flip_Flop d_ff_7 (.clk(Reloj), .D(and_7_out), .Q(Resultado[6]));  // open: Qn, preset, en, reset
  D_Flip_Flop d_ff_8 (.clk(Reloj), .D(and_8_out), .Q(Resultado[7]));  // open: Qn, preset, en, reset

  // Notes on the sheet:
  //   8-Bit Register
endmodule

module Ejercicio3 (
  input  Register_in,
  output [7:0] Resultado
);

  wire Reloj_out;

  Clock Reloj (.out(Reloj_out));
  D_Flip_Flop d_ff_1 (.clk(Reloj_out), .D(Register_in), .Q(Resultado[0]));  // open: Qn, preset, en, reset
  D_Flip_Flop d_ff_2 (.clk(Reloj_out), .D(Resultado[0]), .Q(Resultado[1]));  // open: Qn, preset, en, reset
  D_Flip_Flop d_ff_3 (.clk(Reloj_out), .D(Resultado[1]), .Q(Resultado[2]));  // open: Qn, preset, en, reset
  D_Flip_Flop d_ff_4 (.clk(Reloj_out), .D(Resultado[2]), .Q(Resultado[3]));  // open: Qn, preset, en, reset
  D_Flip_Flop d_ff_5 (.clk(Reloj_out), .D(Resultado[3]), .Q(Resultado[4]));  // open: Qn, preset, en, reset
  D_Flip_Flop d_ff_6 (.clk(Reloj_out), .D(Resultado[4]), .Q(Resultado[5]));  // open: Qn, preset, en, reset
  D_Flip_Flop d_ff_7 (.clk(Reloj_out), .D(Resultado[5]), .Q(Resultado[6]));  // open: Qn, preset, en, reset
  D_Flip_Flop d_ff_8 (.clk(Reloj_out), .D(Resultado[6]), .Q(Resultado[7]));  // open: Qn, preset, en, reset

  // Notes on the sheet:
  //   Shift Register Simulator
endmodule

module Ejercicio4 (
  input  Reloj,
  input  Escribir,
  input  [1:0] Seleccionar_registro_1,
  input  [7:0] EScribir_datos,
  input  [1:0] Escribir_registro,
  input  [1:0] Seleccionar_registro_2,
  output [7:0] Leer_datos_1,
  output [7:0] Leer_datos_2
);

  wire and_1_out, and_2_out, and_3_out, and_4_out, demultiplexer_1_out0, demultiplexer_1_out1,
       demultiplexer_1_out2, demultiplexer_1_out3;
  wire [7:0] ejercicio2_1_resultado, ejercicio2_2_resultado, ejercicio2_3_resultado, ejercicio2_4_resultado;

  Demultiplexer #(.select(2)) demultiplexer_1 (
    .out0(demultiplexer_1_out0), .out1(demultiplexer_1_out1), .out2(demultiplexer_1_out2),
    .out3(demultiplexer_1_out3), .in(Escribir), .sel(Escribir_registro));  // open: en
  and and_1 (and_1_out, demultiplexer_1_out0, Escribir);
  and and_2 (and_2_out, demultiplexer_1_out1, Escribir);
  and and_3 (and_3_out, demultiplexer_1_out2, Escribir);
  and and_4 (and_4_out, demultiplexer_1_out3, Escribir);
  Ejercicio2 ejercicio2_1 (
    .Reloj(Reloj), .Register_in(EScribir_datos), .Control_de_escritura(and_1_out),
    .Resultado(ejercicio2_1_resultado));
  Ejercicio2 ejercicio2_2 (
    .Reloj(Reloj), .Register_in(EScribir_datos), .Control_de_escritura(and_2_out),
    .Resultado(ejercicio2_2_resultado));
  Ejercicio2 ejercicio2_3 (
    .Reloj(Reloj), .Register_in(EScribir_datos), .Control_de_escritura(and_3_out),
    .Resultado(ejercicio2_3_resultado));
  Ejercicio2 ejercicio2_4 (
    .Reloj(Reloj), .Register_in(EScribir_datos), .Control_de_escritura(and_4_out),
    .Resultado(ejercicio2_4_resultado));
  Multiplexer #(.select(2), .width(8)) multiplexer_1 (
    .in0(ejercicio2_1_resultado), .in1(ejercicio2_2_resultado), .in2(ejercicio2_3_resultado),
    .in3(ejercicio2_4_resultado), .out(Leer_datos_1), .sel(Seleccionar_registro_1));  // open: en
  Multiplexer #(.select(2), .width(8)) multiplexer_2 (
    .in0(ejercicio2_1_resultado), .in1(ejercicio2_2_resultado), .in3(ejercicio2_4_resultado),
    .out(Leer_datos_2), .sel(Seleccionar_registro_2));  // open: in2, en

  // Notes on the sheet:
  //   Register Bank
endmodule

// REloj
module Ejercicio5 (
  input  [15:0] Entrada,
  input  in_2,
  output [7:0] operando,
  output out_4,
  output out_5,
  output [1:0] out_6,
  output [1:0] out_7,
  output [1:0] out_8
);

  wire Reloj_out;
  wire [7:0] adder_1_out, ejercicio4_1_leer_datos_1, ejercicio4_1_leer_datos_2, multiplexer_1_out,
       multiplexer_2_out, subtractor_1_out;

  Clock Reloj (.out(Reloj_out));
  Ejercicio4 ejercicio4_1 (
    .Reloj(in_2), .Escribir(Reloj_out), .Seleccionar_registro_1(Entrada[11:10]),
    .EScribir_datos(multiplexer_2_out), .Escribir_registro(Entrada[13:12]),
    .Seleccionar_registro_2(Entrada[9:8]), .Leer_datos_1(ejercicio4_1_leer_datos_1),
    .Leer_datos_2(ejercicio4_1_leer_datos_2));
  Multiplexer #(.width(8)) multiplexer_1 (
    .in0(ejercicio4_1_leer_datos_2), .in1(Entrada[7:0]), .out(multiplexer_1_out), .sel(Entrada[14]));  // open: en
  Adder adder_1 (.a(ejercicio4_1_leer_datos_1), .b(multiplexer_1_out), .out(adder_1_out));  // open: cin, cout
  Subtractor subtractor_1 (
    .a(ejercicio4_1_leer_datos_1), .b(multiplexer_1_out), .out(subtractor_1_out));  // open: bin, bout
  Multiplexer #(.width(8)) multiplexer_2 (
    .in0(adder_1_out), .in1(subtractor_1_out), .out(multiplexer_2_out), .sel(Entrada[15]));  // open: en
  Hex_Digit_Display hex_digit_display_1 (.value(multiplexer_2_out[7:4]));  // open: dp
  Hex_Digit_Display hex_digit_display_2 (.value(multiplexer_2_out[3:0]));  // open: dp

  assign operando = Entrada[7:0];
  assign out_4 = Entrada[15];
  assign out_5 = Entrada[14];
  assign out_6 = Entrada[13:12];
  assign out_7 = Entrada[9:8];
  assign out_8 = Entrada[11:10];

  // Notes on the sheet:
  //   Adder/Substractor
  //   Banco de datos
  //   código de operación : 0 registro, 1 inmediato
  //   Inmediato entero 
  //   para el segundo
  //   Registro resultado
  //   Registro operando 2
  //   Registro operando 1
  //   código de operación 0 +, 1 -
endmodule
